// Logisim project upper2.circ as structural Verilog: 1 circuit, main circuit main
module main (
);

  wire and_1_out, and_2_out, and_3_out, and_4_out, and_5_out, and_6_out, and_7_out, and_8_out, not_1_out,
       not_2_out, not_3_out, not_4_out, not_5_out, not_6_out, not_7_out, not_8_out, or_1_out, or_2_out,
       or_3_out, or_4_out, or_5_out, or_6_out, or_7_out, or_8_out;

  not not_1 (not_1_out, 1'b0);
  not not_2 (not_2_out, 1'b1);
  not not_3 (not_3_out, 1'b1);
  not not_4 (not_4_out, 1'b0);
  not not_5 (not_5_out, 1'b1);
  not not_6 (not_6_out, 1'b1);
  not not_7 (not_7_out, 1'b1);
  not not_8 (not_8_out, 1'b0);
  and and_1 (and_1_out, 1'b1, 1'b1);
  and and_2 (and_2_out, not_5_out, not_7_out);
  and and_3 (and_3_out, not_8_out, 1'b0);
  and and_4 (and_4_out, not_3_out, 1'b0);
  and and_5 (and_5_out, 1'b0, 1'b1);
  and and_6 (and_6_out, not_6_out, 1'b1);
  and and_7 (and_7_out, not_2_out, not_1_out);
  and and_8 (and_8_out, not_4_out, 1'b1);
  // Probe on or_1_out
  or or_1 (or_1_out, and_4_out, and_2_out);
  // Probe on or_2_out
  or or_2 (or_2_out, and_1_out, and_8_out);
  or or_3 (or_3_out, and_7_out, and_5_out);
  // Probe on or_3_out
  or or_4 (or_4_out, and_3_out, and_6_out);
  // Probe on or_4_out
  // Probe on or_5_out
  or or_5 (or_5_out, and_2_out, and_7_out);
  // Probe on or_6_out
  or or_6 (or_6_out, and_3_out, and_5_out);
  or or_7 (or_7_out, and_4_out, and_2_out);
  // Probe on or_7_out
  or or_8 (or_8_out, and_7_out, and_6_out);
  // Probe on or_8_out

  // Notes on the sheet:
  //   0
  //   1
  //   1
  //   0
  //   'n'
  //   1
  //   1
  //   1
  //   0
  //   x0
  //   x7
  //   0
  //   1
  //   0
  //   0
  //   0
  //   0
  //   0
  //   0
  //   '@'
endmodule
